# Fritzing sketch circuit (saved by Fritzing 0.9.3b)
breadboards: 1

parts:
  Part1 = Arduino Uno (Rev3)
  LED1 = LED - 5mm [color="Red (633nm)" package="5 mm [THT]"]
  LED2 = LED - 5mm [color="Red (633nm)" package="5 mm [THT]"]
  R3 = Resistor [tolerance=±5% resistance=220 package=THT]
  R10 = Resistor [tolerance=±5% resistance=220 package=THT]

nets:
  N1: Part1.D10_PWM/SS, LED2.anode
  N2: Part1.D11_PWM/MOSI, LED1.anode
  N3: Part1.GND, R3.Pin_1, R10.Pin_1
  N4: LED1.cathode, R10.Pin_0
  N5: LED2.cathode, R3.Pin_0
