# Fritzing sketch circuit (saved by Fritzing 0.9.3b)
breadboards: 1

parts:
  Part1 = Arduino Uno (Rev3)
  T1 = TMP36 Temperature Sensor [package="TO92 [THT]"]
  J1 = Basic Servo

nets:
  N1: Part1.A1, T1.Vout
  N2: Part1.D9_PWM, J1.pulse
  5V: Part1.5V, T1.+Vs, J1.vcc
  GND: Part1.GND, T1.GND
