# Fritzing sketch circuit (saved by Fritzing 0.9.3b)
breadboards: 1

parts:
  Part1 = Arduino Uno (Rev3)
  R11 = Resistor [tolerance=±5% resistance=10k package=THT]
  S2 = Pushbutton [package="[THT]"]
  LED1 = LED - 5mm [color="Red (633nm)" package="5 mm [THT]"]
  R10 = Resistor [tolerance=±5% resistance=220 package=THT]

nets:
  N1: Part1.D11_PWM/MOSI, LED1.anode
  N2: Part1.D13/SCK, R11.Pin_1, S2.Pin_1, S2.Pin_2
  N3: Part1.5V, R11.Pin_0
  N4: Part1.GND, R10.Pin_1
  N5: S2.Pin_3, S2.Pin_4
  N6: LED1.cathode, R10.Pin_0
