# Fritzing sketch circuit (saved by Fritzing 0.9.3b)
breadboards: 1

parts:
  Part1 = Arduino Uno (Rev3)
  LED1 = LED - 5mm [color="Red (633nm)" package="5 mm [THT]"]
  S1 = Pushbutton [package="[THT]"]
  S2 = Pushbutton [package="[THT]"]
  R10 = Resistor [tolerance=±5% resistance=220 package=THT]
  R11 = Resistor [tolerance=±5% resistance=10k package=THT]
  R12 = Resistor [tolerance=±5% resistance=10k package=THT]

nets:
  N1: Part1.D11_PWM/MOSI, LED1.anode
  N2: Part1.D12/MISO, S1.Pin_1, S1.Pin_2, R12.Pin_1
  N3: Part1.D13/SCK, S2.Pin_1, S2.Pin_2, R11.Pin_1
  N4: Part1.5V, R11.Pin_0, R12.Pin_0
  N5: Part1.GND, R10.Pin_1
  N6: LED1.cathode, R10.Pin_0
  N7: S1.Pin_3, S1.Pin_4, S2.Pin_3, S2.Pin_4
