# Fritzing sketch circuit (saved by Fritzing 0.9.3b)
breadboards: 1

parts:
  Part1 = Arduino Uno (Rev3)
  LED1 = LED - 5mm [color="Red (633nm)" package="5 mm [THT]"]
  R10 = Resistor [tolerance=±5% resistance=220 package=THT]
  R7 = Resistor [tolerance=±5% resistance=10k package=THT]
  R2 = Photocell (LDR) [package=THT]

nets:
  N1: Part1.A2, R7.Pin_1, R2.pin_0
  N2: Part1.D11_PWM/MOSI, LED1.anode
  N3: Part1.5V, R2.pin_1
  N4: Part1.GND, R10.Pin_1
  N5: LED1.cathode, R10.Pin_0
