# Fritzing sketch circuit (saved by Fritzing 0.9.3b)
breadboards: 1

parts:
  Part1 = Arduino Uno (Rev3)
  R7 = Resistor [tolerance=±5% resistance=10k package=THT]
  R2 = Photocell (LDR) [package=THT]
  J1 = Basic Servo

nets:
  N1: Part1.A2, R7.Pin_1, R2.pin_0
  N2: Part1.D9_PWM, J1.pulse
  5V: Part1.5V, R2.pin_1, J1.vcc
  N3: R7.Pin_0, J1.gnd
