# Fritzing sketch circuit (saved by Fritzing 0.9.3b)
breadboards: 1

parts:
  Part1 = Arduino Uno (Rev3)
  T1 = TMP36 Temperature Sensor [package="TO92 [THT]"]
  LCD1 = LCD screen
  R2 = Trimmer Potentiometer [maximum_resistance=10kΩ package=THT]

nets:
  N1: Part1.A1, T1.Vout
  N2: Part1.D11_PWM/MOSI, LCD1.RS
  N3: Part1.D12/MISO, LCD1.E
  N4: Part1.D2, LCD1.DB4
  N5: Part1.D3_PWM, LCD1.DB5
  N6: Part1.D4, LCD1.DB6
  N7: Part1.D5_PWM, LCD1.DB7
  5V: Part1.5V, T1.+Vs, LCD1.VDD, LCD1.LED+, R2.leg1
  GND: Part1.GND, T1.GND, LCD1.VSS, LCD1.R/W, LCD1.LED-, R2.leg2
  N8: LCD1.V0, R2.wiper
