# Fritzing sketch circuit (saved by Fritzing 0.9.3b)
breadboards: 1

parts:
  Part1 = Arduino Uno (Rev3)
  T1 = TMP36 Temperature Sensor [package="TO92 [THT]"]
  LCD1 = LCD screen
  R2 = Trimmer Potentiometer [maximum_resistance=10kΩ package=THT]
  R3 = Photocell (LDR) [package=THT]
  R8 = Resistor [tolerance=±5% resistance=10k package=THT]

nets:
  N1: Part1.A0, R3.pin_1, R8.Pin_0
  N2: Part1.A1, T1.Vout
  N3: Part1.D11_PWM/MOSI, LCD1.RS
  N4: Part1.D12/MISO, LCD1.E
  GND: Part1.GND, T1.GND, LCD1.VSS, LCD1.R/W, LCD1.LED-, R2.leg2, R8.Pin_1
  N5: Part1.D2, LCD1.DB4
  N6: Part1.D3_PWM, LCD1.DB5
  N7: Part1.D4, LCD1.DB6
  N8: Part1.D5_PWM, LCD1.DB7
  5V: Part1.5V, T1.+Vs, LCD1.VDD, LCD1.LED+, R2.leg1, R3.pin_0
  N9: LCD1.V0, R2.wiper
