# Fritzing sketch ldr-led (saved by Fritzing 0.9.3b)
breadboards: 1

parts:
  Part1 = Arduino Uno (Rev3)
  R1 = Photocell (LDR) [package=THT]
  R2 = Resistor [tolerance=±5% resistance=100k package="2512 [SMD]"]
  LED1 = LED - 5mm [color="Red (633nm)" package="5 mm [THT]"]
  R3 = Resistor [tolerance=±5% resistance=220 package=THT]

nets:
  N1: Part1.A0, R1.pin_1, R2.Pin_0
  N2: Part1.D3_PWM, LED1.anode
  N3: Part1.5V, R1.pin_0
  N4: Part1.GND, R2.Pin_1, R3.Pin_0
  N5: LED1.cathode, R3.Pin_1
