# Fritzing sketch pot-led (saved by Fritzing 0.9.3b)
breadboards: 1

parts:
  Part1 = Arduino Uno (Rev3)
  LED1 = LED - 5mm [color="Red (633nm)" package="5 mm [THT]"]
  R3 = Resistor [tolerance=±5% resistance=220 package=THT]
  R4 = Rotary Potentiometer (Large) [maximum_resistance=100kΩ package=THT]

nets:
  N1: Part1.A0, R4.wiper
  N2: Part1.D3_PWM, LED1.anode
  N3: Part1.5V, R4.leg1
  N4: Part1.GND, R3.Pin_0, R4.leg2
  N5: LED1.cathode, R3.Pin_1
